# Fritzing sketch simpleinfrared (saved by Fritzing 0.8.7b)
breadboards: 1

parts:
  IR1 = TSOP312.., 314.. [package=THT]
  LED1 = LED - 5mm [color="Red (633nm)" package="5 mm [THT]"]
  R1 = Resistor [tolerance=±5% resistance=2.2k package=THT]
  Bauteil1 = Arduino Uno (Rev3)
  R2 = Resistor [tolerance=±5% resistance=220 package=THT]

nets:
  N1: IR1.GND, Bauteil1.D3_PWM
  N2: IR1.Vs, LED1.cathode, Bauteil1.GND
  N3: IR1.Data, R1.Pin_0
  N4: LED1.anode, R2.Pin_0
  N5: R1.Pin_1, Bauteil1.5V
  N6: Bauteil1.D12/MISO, R2.Pin_1
